# Fritzing sketch Project_vxl_v1 (saved by Fritzing 1.0.4)
circuit board: 8.46667cm x 5.64444cm
breadboards: 2

parts:
  Mod1 = SDS011 - dust sensor [part_number=1]
  M3 = DOIT Esp32 DevKit v1 (30 pins long, 11 pins width) [part_number=ESP32S-PIN30]
  OLED_I2C2 = OLED 128x64 I2C Monochrome Display
  microSD2 = MicroSD Card Module
  M4 = BME280

nets:
  5V: Mod1.5V, M3.VIN
  GND: Mod1.GND, M3.GND, OLED_I2C2.GND, microSD2.GND, M4.GND
  N1: Mod1.RXD, M3.TX0
  N2: Mod1.TXD, M3.RX0
  3V3: M3.3V3, OLED_I2C2.VDD, microSD2.VCC, M4.VIN
  N3: M3.D5, microSD2.CS
  N4: M3.D18, microSD2.SCK
  N5: M3.D19, microSD2.MISO
  N6: M3.D21, M3.D22, OLED_I2C2.SDA, OLED_I2C2.SCK, M4.SCL, M4.SDA
  N7: M3.D23, microSD2.MOSI

custom parts:
  SDS011 - dust sensor: The SDS 011 Sensor is a quite recent Air Quality Sensor developed by inovafit, a spin-off from the university of Jinan (in Shandong). With its size, it is probably one of the best sensor in terms of accuracy: While other sensors tend to focus on shrinking the sensor size, the SDS 011 has opted for a size tradeoff allowing it to use a larger fan. And the larger the fan, the better the quality.
  DOIT Esp32 DevKit v1 (30 pins long, 11 pins width): The DOIT Esp32 DevKit v1 is one of the development board created by DOIT to evaluate the ESP-WROOM-32 module. It is based on the ESP32 microcontroller that boasts Wifi, Bluetooth, Ethernet and Low Power support all in a single chip. (vanepp) made breadboard work, adjusted pin numbering and labels and reduced size of schematic and cleaned up pcb. This chip is 30pins long (2 x15) and 11 pins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
  MicroSD Card Module: A common microSD card module.
  BME280: Temperature Humidity Barometric presure Sensor

// code stored in the sketch: Untitled2.bas
#include <Wire.h>
#include <Adafruit_GFX.h>
#include <Adafruit_SSD1306.h>

#define SCREEN_WIDTH 128
#define SCREEN_HEIGHT 64
#define OLED_RESET    -1
#define OLED_ADDR     0x3C   // ph? bi?n: 0x3C ho?c 0x3D

Adafruit_SSD1306 display(SCREEN_WIDTH, SCREEN_HEIGHT, &Wire, OLED_RESET);

void setup() {#include <Wire.h>
#include <SPI.h>
#include <SD.h>

#include <Adafruit_GFX.h>
#include <Adafruit_SH110X.h>
#include <Adafruit_SHT31.h>
#include <Adafruit_BME280.h>

#include "SdsDustSensor.h"

/* ================= OLED SH1106 ================= */
#define SCREEN_WIDTH 128
#define SCREEN_HEIGHT 64
Adafruit_SH1106G display(SCREEN_WIDTH, SCREEN_HEIGHT, &Wire, -1);

/* ================= SDS011 ================= */
HardwareSerial mySerial(2);
SdsDustSensor sds(mySerial);

/* ================= SHT31 ================= */
Adafruit_SHT31 sht31 = Adafruit_SHT31();

/* ================= BME280 ================= */
Adafruit_BME280 bme;

/* ================= SD Card ================= */
#define SD_CS 5
File dataFile;

/* ================= TIME ================= */
unsigned long lastSave = 0;
const unsigned long interval = 5000; // 5 giây

void setup() {
  Serial.begin(9600);

  /* ---------- I2C ---------- */
  Wire.begin(21, 22);

  /* ---------- OLED ---------- */
  delay(200);
  if (!display.begin(0x3C, true)) {
    Serial.println("OLED FAIL");
    while (1);
  }
  display.clearDisplay();
  display.display();

  /* ---------- SDS011 ---------- */
  mySerial.begin(9600, SERIAL_8N1, 16, 17);
  sds.begin();
  sds.wakeup();
  sds.setActiveReportingMode();
  sds.setContinuousWorkingPeriod();

  /* ---------- SHT31 ---------- */
  if (!sht31.begin(0x44)) {
    Serial.println("SHT31 FAIL");
  }

  /* ---------- BME280 ---------- */
  if (!bme.begin(0x76)) {
    Serial.println("BME280 FAIL");
  }

  /* ---------- SD Card ---------- */
  if (!SD.begin(SD_CS)) {
    Serial.println("SD FAIL");
    while (1);
  }

  Serial.println("SYSTEM READY");
}

void loop() {

  /* ---------- SDS011 ---------- */
  PmResult pm = sds.readPm();

  /* ---------- SHT31 ---------- */
  float shtTemp = sht31.readTemperature();
  float shtHumi = sht31.readHumidity();

  /* ---------- BME280 ---------- */
  float bmeTemp  = bme.readTemperature();
  float bmeHumi  = bme.readHumidity();
  float bmePress = bme.readPressure() / 100.0; // Pa ? hPa

  /* ---------- OLED ---------- */
  display.clearDisplay();
  display.setTextSize(1);
  display.setTextColor(SH110X_WHITE);

  display.setCursor(0, 0);
  display.print("T SHT:");
  display.print(shtTemp, 1);
  display.print(" BME:");
  display.print(bmeTemp, 1);

  display.setCursor(0, 12);
  display.print("H SHT:");
  display.print(shtHumi, 1);
  display.print(" BME:");
  display.print(bmeHumi, 1);

  display.setCursor(0, 24);
  display.print("P BME:");
  display.print(bmePress, 1);
  display.print(" hPa");

  if (pm.isOk()) {
    display.setCursor(0, 40);
    display.print("PM2.5: ");
    display.print(pm.pm25);

    display.setCursor(0, 52);
    display.print("PM10 : ");
    display.print(pm.pm10);
  } else {
    display.setCursor(0, 40);
    display.print("SDS011 ERROR");
  }

  display.display();

  /* ---------- SERIAL MONITOR (GI?NG OLED) ---------- */
  Serial.println();
  Serial.print("T SHT:");
  Serial.print(shtTemp, 1);
  Serial.print(" BME:");
  Serial.println(bmeTemp, 1);

  Serial.print("H SHT:");
  Serial.print(shtHumi, 1);
  Serial.print(" BME:");
  Serial.println(bmeHumi, 1);

  Serial.print("P BME:");
  Serial.print(bmePress, 1);
  Serial.println(" hPa");

  if (pm.isOk()) {
    Serial.print("PM2.5: ");
    Serial.println(pm.pm25);
    Serial.print("PM10 : ");
    Serial.println(pm.pm10);
  } else {
    Serial.println("SDS011 ERROR");
  }

  /* ---------- SD LOG ---------- */
  if (pm.isOk() && millis() - lastSave >= interval) {
    lastSave = millis();

    dataFile = SD.open("/dust_log.csv", FILE_APPEND);
    if (dataFile) {
      dataFile.print(millis() / 1000);
      dataFile.print(",");
      dataFile.print(pm.pm25);
      dataFile.print(",");
      dataFile.print(pm.pm10);
      dataFile.print(",");
      dataFile.print(shtTemp);
      dataFile.print(",");
      dataFile.print(shtHumi);
      dataFile.print(",");
      dataFile.print(bmeTemp);
      dataFile.print(",");
      dataFile.print(bmeHumi);
      dataFile.print(",");
      dataFile.println(bmePress);
      dataFile.close();
    }
  }

  delay(1000);
}

  Wire.begin(21, 22); // SDA, SCL
  if(!display.begin(SSD1306_SWITCHCAPVCC, OLED_ADDR)) {
    Serial.println("OLED not found");
    while(true);
  }
  display.clearDisplay();
  display.setTextSize(2);
  display.setTextColor(SSD1306_WHITE);
  display.setCursor(0, 0);
  display.println("ESP32");
  display.println("OLED OK!");
  display.display();
}

void loop() {}
